# Fritzing sketch variometer (saved by Fritzing 0.9.3b)
breadboards: 1

parts:
  U1 = LIPO-2000mAh [package=lipo-2000]
  S1 = JOYSTICK_MINI [package=joystick_mini]
  U2 = NodeMCU V1.0
  10DOF_(gyro_accel_and_barometer) = CJMCU-10DOF [form="♀ (female)" package=THT]
  MicroSD = MicroSD Card Module
  Composant3 = Adafruit 2.0 inch 240x320 IPS TFT [part_number="Adafruit #4311"]
  Composant4 = Adafruit Pro Trinket LiIon/LiPoly Backpack [part_number="Adafruit #2124"]
  Buck_Converter = Mini-360 DC-DC Buck converter [package=THT]
  GPS_(BN280_will_be_used) = SUP500F [package=sup500f]
  R3 = Resistor [tolerance=±5% resistance=1k package="0805 [SMD]"]
  R4 = Resistor [tolerance=±5% resistance=10k package="0805 [SMD]"]
  R5 = Resistor [tolerance=±5% resistance=22k package="0805 [SMD]"]
  R6 = Resistor [tolerance=±5% resistance=47k package="0805 [SMD]"]
  R7 = Resistor [tolerance=±5% resistance=68k package="0805 [SMD]"]
  R8 = Resistor [tolerance=±5% resistance=4.7k package="0805 [SMD]"]
  R9 = Resistor [tolerance=±5% resistance=4.7k package="0805 [SMD]"]

nets:
  N1: U1.+, Composant4.VBAT
  GND: U1.-, S1.GND, Composant3.GND, Composant4.GND, Buck_Converter.IN-, GPS_(BN280_will_be_used).GND
  N2: S1.UP, R5.Pin_0
  N3: S1.RIGHT, R6.Pin_0
  N4: S1.LEFT, R7.Pin_0
  N5: S1.CENT, R4.Pin_0
  N6: S1.DOWN, R3.Pin_0
  N7: U2.D0, GPS_(BN280_will_be_used).PPS
  N8: U2.D3, 10DOF_(gyro_accel_and_barometer).SCL, R9.Pin_0
  N9: U2.D4, 10DOF_(gyro_accel_and_barometer).SDA, R8.Pin_0
  GND_2: U2.GND, 10DOF_(gyro_accel_and_barometer).GND, 10DOF_(gyro_accel_and_barometer).AD0, MicroSD.GND, Buck_Converter.OUT-
  N10: U2.D5, MicroSD.SCK, Composant3.SCLK_5V
  N11: U2.D6, MicroSD.MISO, Composant3.MISO
  N12: U2.D7, MicroSD.MOSI, Composant3.MOSI_5V
  N13: U2.D8, MicroSD.CS, Composant3.LCDCS_5V
  N14: U2.RX, GPS_(BN280_will_be_used).TX-O
  N15: U2.TX, GPS_(BN280_will_be_used).RX-I
  VIN: U2.Vin, Composant3.VIN, Composant4.VBUS, Buck_Converter.IN+
  N16: U2.A0, R4.Pin_1, R5.Pin_1, R6.Pin_1, R7.Pin_1
  +3V3: 10DOF_(gyro_accel_and_barometer).+3V3, MicroSD.VCC, Buck_Converter.OUT+, R8.Pin_1, R9.Pin_1

custom parts:
  NodeMCU V1.0: ESP8266 based NodeMCU
  CJMCU-10DOF: Placa CJMCU 10DOF basada en conjunto de acelerómetro+giroscopios+magnetómetro MPU-9250 y un barómetro BMP180
  Adafruit 2.0 inch 240x320 IPS TFT: This gorgeous IPS display breakout is the best way to add a small, colorful and bright display to any project, with excellent visibility from any angle. Since the display uses 4-wire SPI to communicate and has its own pixel-addressable frame buffer, it can be used with every kind of microcontroller. Even a very small one with low memory and few pins available! The 2.0" display has 320x240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
  Adafruit Pro Trinket LiIon/LiPoly Backpack: If you have a Pro Trinket you probably know it's the perfect little size for a portable project. This LiPoly backpack makes it really easy to do! Instead of wiring 2 or 3 boards together to make a charging system, this little PCB sits on top of the Pro Trinket and allows a LiPoly/LiIon battery to plug in. When the Pro Trinket USB port is powered, the battery is recharged automatically. Unplug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
  Mini-360 DC-DC Buck converter: Mini-360 DC-DC Buck converter. Tiny buck step down voltage converter, input voltage 4.75 to 23V output 1 to 17V adjustable. Available from ebay and the like.
